// Logisim project Atividade1.circ as structural Verilog: 1 circuit, main circuit main
module main (
  input  in_1,
  input  A,
  input  in_3,
  input  B,
  input  in_5,
  input  C,
  input  D,
  input  in_8,
  input  in_9,
  input  S,
  input  in_11,
  input  in_12,
  input  in_13,
  input  R,
  input  in_15,
  input  in_16,
  input  in_17,
  output out_18,
  output out_19,
  output out_20,
  output out_21,
  output Q,
  output out_23,
  output QQ,
  output out_25,
  output out_26
);

  wire nand_2_out, nand_3_out;

  not not_1 (out_20, in_5);
  and and_1 (out_18, in_1, in_3);
  or or_1 (out_21, in_8, in_9);
  nand nand_1 (out_23, in_11, in_12);
  nor nor_1 (out_25, in_13, in_15);
  xor xor_1 (out_26, in_16, in_17);
  nand nand_2 (nand_2_out, A, B);
  nand nand_3 (nand_3_out, C, D);
  nand nand_4 (Q, S, QQ);
  nand nand_5 (QQ, Q, R);
  or or_2 (out_19, nand_2_out, nand_3_out);

  // Notes on the sheet:
  //   And
  //   Not
  //   Or
  //   Nand
  //   Nor
  //   Xor
  //   (A NAND B) OR (C NAND D)
  //   Latch SR com portas NAND
endmodule
