// Logisim project CircuitoDisparaAlarmeCarro.circ as structural Verilog: 1 circuit, main circuit main
module main (
  input  I,
  input  M,
  input  C,
  output out_4
);

  wire and_1_out, and_2_out, and_3_out, not_1_out, not_2_out;

  not not_1 (not_1_out, C);
  not not_2 (not_2_out, I);
  and and_1 (and_1_out, I, not_1_out);
  and and_2 (and_2_out, not_2_out, M);
  and and_3 (and_3_out, M, not_1_out);
  or or_1 (out_4, and_1_out, and_2_out, and_3_out);
endmodule
