// Logisim project Reg8.circ as structural Verilog: 1 circuit, main circuit main
module main (
  input  in_1,
  input  in_2,
  output out_3,
  output out_4,
  output out_5
);

  wire CLK_out, D1_q, D2_q, D3_q, D4_q, D5_q, D6_q, D7_q;

  Clock CLK (.out(CLK_out));
  D_Flip_Flop D7 (.D(in_2), .clk(CLK_out), .Q(D7_q));  // open: Qn, preset, reset
  D_Flip_Flop d_ff_1 (.D(in_1), .clk(CLK_out), .Q(out_3));  // open: Qn, preset, reset
  D_Flip_Flop D6 (.D(D7_q), .clk(CLK_out), .Q(D6_q));  // open: Qn, preset, reset
  D_Flip_Flop d_ff_2 (.D(out_3), .clk(CLK_out), .Q(out_4));  // open: Qn, preset, reset
  D_Flip_Flop D5 (.D(D6_q), .clk(CLK_out), .Q(D5_q));  // open: Qn, preset, reset
  D_Flip_Flop D4 (.D(D5_q), .clk(CLK_out), .Q(D4_q));  // open: Qn, preset, reset
  D_Flip_Flop D3 (.D(D4_q), .clk(CLK_out), .Q(D3_q));  // open: Qn, preset, reset
  D_Flip_Flop D2 (.D(D3_q), .clk(CLK_out), .Q(D2_q));  // open: Qn, preset, reset
  D_Flip_Flop D1 (.D(D2_q), .clk(CLK_out), .Q(D1_q));  // open: Qn, preset, reset
  D_Flip_Flop D0 (.D(D1_q), .clk(CLK_out), .Q(out_5));  // open: Qn, preset, reset
endmodule
