// Logisim project CircuitoElevador.circ as structural Verilog: 1 circuit, main circuit main
module main (
  input  D,
  input  U,
  input  L,
  output UP,
  output DOWN
);

  wire not_1_out;

  not not_1 (not_1_out, U);
  and and_1 (UP, D, U);
  and and_2 (DOWN, D, not_1_out, L);
endmodule
